# Fritzing sketch 2 (saved by Fritzing 0.9.4)
breadboards: 12

parts:
  S1 = SPST Switch [package=switch-spdt]
  LED1 = smd LED [color="Red (633nm)" package="1206 [SMD]"]
  S3 = SPST Switch [package=switch-spdt]
  S4 = SPST Switch [package=switch-spdt]
  S5 = SPST Switch [package=switch-spdt]
  S6 = SPST Switch [package=switch-spdt]
  S7 = SPST Switch [package=switch-spdt]
  S8 = SPST Switch [package=switch-spdt]
  S9 = SPST Switch [package=switch-spdt]
  S10 = SPST Switch [package=switch-spdt]
  VCC1 = Battery
  Part1 = Analog Digital MUX Breakout
  Part2 = Analog Digital MUX Breakout
  Part3 = Analog Digital MUX Breakout
  Part4 = Analog Digital MUX Breakout
  Part5 = Analog Digital MUX Breakout
  U2 = 74HC04_HEX_INVERTER [package=dil14]
  S11 = SPST Switch [package=switch-spdt]
  S12 = SPST Switch [package=switch-spdt]
  S13 = SPST Switch [package=switch-spdt]
  S14 = SPST Switch [package=switch-spdt]
  IC2 = 74HC08 Logic AND Gate [part_number=74HC08 package="DIP (Dual Inline) [THT]"]
  IC3 = DIP - 14 pins [chip_label=74LS86 package="DIP (Dual Inline) [THT]"]
  U3 = SN74LS32N [package="DIP14 [THT]"]
  U4 = 74HC04_HEX_INVERTER [package=dil14]
  VCC2 = Battery
  R1 = Resistor [tolerance=±5% resistance=10k package="1206 [SMD]"]
  R2 = Resistor [tolerance=±5% resistance=10k package="1206 [SMD]"]
  R3 = Resistor [tolerance=±5% resistance=10k package="1206 [SMD]"]
  R4 = Resistor [tolerance=±5% resistance=10k package="1206 [SMD]"]
  R5 = Resistor [tolerance=±5% resistance=10k package="1206 [SMD]"]
  LED2 = smd LED [color="Red (633nm)" package="1206 [SMD]"]
  LED3 = smd LED [color="Red (633nm)" package="1206 [SMD]"]
  LED4 = smd LED [color="Red (633nm)" package="1206 [SMD]"]
  LED5 = smd LED [color="Red (633nm)" package="1206 [SMD]"]

nets:
  VCC: S1.O, S3.O, S4.O, S5.O, S6.O, S7.O, S8.O, S9.O, S10.O, VCC1.+, U2.VCC, S11.S, S12.S, S13.S, S14.S, IC2.VCC, IC3.VCC, U3.Vcc, U4.VCC
  GND: S1.S, S3.S, S4.S, S5.S, S6.S, S7.S, S8.S, S9.S, S10.S, VCC1.-, U2.GND, S11.O, S12.O, S13.O, S14.O, IC2.GND, IC3.GND, U3.GND, U4.GND
  GND_2: LED1.cathode, Part1.C12, Part1.C13, Part1.C14, Part1.C15, Part1.GND, Part1.EN, Part2.C4, Part2.C5, Part2.C6, Part2.C7, Part2.C8, Part2.C9, Part2.C12, Part2.C13, Part2.C14, Part2.C15, Part2.GND, Part2.EN, Part3.GND, Part3.EN, Part4.GND, Part4.EN, Part5.GND, Part5.EN, VCC2.-, LED4.cathode, LED5.cathode
  N1: LED1.anode, R2.Pin_1
  N2: S6.P, U2.6A
  N3: S7.P, U2.5A
  N4: S8.P, U2.4A
  N5: S9.P, U2.1A
  VCC_2: Part1.VCC, Part2.VCC, Part3.VCC, Part5.VCC, VCC2.+
  N6: Part1.S0, Part2.S0, Part3.S0, Part4.S0, Part5.S0, S14.P
  N7: Part1.S1, Part2.S1, Part3.S1, Part4.S1, Part5.S1, S13.P
  N8: Part1.S2, Part2.S2, Part3.S2, Part4.S2, Part5.S2, S12.P
  N9: Part1.S3, Part2.S3, Part3.S3, Part4.S3, Part5.S3, S11.P
  N10: Part1.SIG, R3.Pin_0
  N11: Part2.SIG, R2.Pin_0
  N12: Part3.SIG, R1.Pin_0
  N13: Part4.SIG, R4.Pin_0
  N14: Part5.SIG, R5.Pin_0
  N15: R1.Pin_1, LED4.anode
  N16: R3.Pin_1, LED2.anode
  N17: R4.Pin_1, LED3.anode
  N18: R5.Pin_1, LED5.anode
  N19: LED2.cathode, LED3.cathode

notes:
  since no 4008 IC existed in fritzing, consider these below as full adders which pins and thir order where shown in proteus
  select unit
  Cin
  B same as A
  A top to buttom S0 to S3

custom parts:
  DIP - 14 pins: A DIP stand-in part for whatever IC you want. With 14 pins on a 300mil dual inline package (DIP) footprint.
